# Fritzing sketch conexion_laberinto (saved by Fritzing 0.9.10b)

parts:
  Part1 = Arduino Uno (Rev3) - ICSP
  L298N1 = L298N DC motor driver
  Part2 = SRF05 Ultrasonic Rangefinder
  Part3 = SRF05 Ultrasonic Rangefinder
  Part4 = SRF05 Ultrasonic Rangefinder
  M1 = gear-motor
  M2 = gear-motor
  BAT1 = BC9VPC [package=bc9vpc]

nets:
  N1: Part1.D8, L298N1.IN1
  N2: Part1.D9_PWM, L298N1.IN2
  N3: Part1.D10_PWM/SS, L298N1.IN3
  N4: Part1.D11_PWM/MOSI, L298N1.IN4
  N5: Part1.D2, Part2.Trig
  N6: Part1.D3_PWM, Part2.Echo
  N7: Part1.D4, Part3.Trig
  N8: Part1.D5_PWM, Part3.Echo
  N9: Part1.D6_PWM, Part4.Trig
  N10: Part1.D7, Part4.Echo
  GND: Part1.GND, L298N1.GND, Part2.GND, Part3.GND, BAT1.V-
  VIN: Part1.VIN, L298N1.5V
  N11: L298N1.OUT1, M1.pin_2
  N12: L298N1.OUT2, M1.pin_1
  N13: L298N1.OUT3, M2.pin_2
  N14: L298N1.OUT4, M2.pin_1
  N15: L298N1.12V, BAT1.V+

notes:
  izquierda
  Derecha

custom parts:
  L298N DC motor driver: 2x DC motor driver with 78M05 positive voltage regulator (7..35 V) L298N: max 46 V, 2 A Set 5 V Enable jumper to enable 5 V regultor (needed for the L298N) and +5 V output at screw terminal or supply external +5 V at screw terminal Set ENA and/or ENB to +5 V to enable motor permanently or supply ENA and/or ENB with PWM signal IN1 and IN2 set rotation directory for motor A (OUT1/OUT2) IN2 and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
